# Fritzing sketch vc_board (saved by Fritzing 0.7.12b)
breadboards: 1

parts:
  IC1 = IC, DIP package, 8 pins [chip_label=ATtiny85]
  U1 = Voltage Regulator - 5V [package="TO220 [THT]"]
  R1 = Rotary Potentiometer (Small) [maximum_resistance=100kΩ]
  S1 = Pushbutton [package="[THT]"]
  J1 = Piezo Speaker
  9V_Battery = DC Power [voltage=5]

nets:
  N1: IC1.pin1, S1.Pin_3, S1.Pin_4
  N2: IC1.pin2, R1.leg2
  N3: IC1.pin3, R1.wiper
  GND: IC1.pin4, U1.GND, R1.leg1, S1.Pin_1, S1.Pin_2, 9V_Battery.GND
  N4: IC1.pin5, J1.pin2
  N5: IC1.pin6, J1.pin1
  N6: IC1.pin8, U1.output_voltage
  N7: U1.input_voltage, 9V_Battery.V+
